# Fritzing sketch bogus_finger_electronics (saved by Fritzing 0.8.7b)
breadboards: 1

parts:
  U1 = HEF4543 [package=dil16]
  R1 = Resistor [tolerance=±5% resistance=43 package=THT]
  Componente2 = Arduino Mega Proto Shield (v6)
  Componente3 = DeuLigne 1.1 - The Snootlab's LCD shield for Arduino
  S1 = Pushbutton [package="[THT]"]
  S2 = Pushbutton [package="[THT]"]
  S3 = Pushbutton [package="[THT]"]
  S4 = Toggle Switch [package=THT]

nets:
  +5V: U1.LD, Componente2.+5V, Componente2.N$95, Componente3.+5V
  N1: U1.D2, Componente2.N$94
  GND: U1.D1, U1.D0, Componente2.GND, Componente2.N$234, Componente2.N$273, Componente2.N$315, Componente3.GND, S1.Pin_3, S1.Pin_4, S2.Pin_3, S2.Pin_4, S3.Pin_3, S3.Pin_4, S4.COM
  N2: U1.D3, U1.F, Componente2.AREF, Componente2.N$143, Componente2.N$289, Componente2.N$314
  N3: U1.PH, Componente2.N$281
  N4: U1.BL, Componente2.N$282
  N5: U1.GND, R1.Pin_1, Componente2.N$295
  N6: U1.A, R1.Pin_0, Componente2.N$267
  N7: U1.B, Componente2.N$268
  N8: U1.C, Componente2.N$239
  N9: U1.D, Componente2.N$236
  N10: U1.E, Componente2.N$235
  N11: U1.G, Componente2.N$251
  N12: U1.VCC, Componente2.N$135
  N13: Componente2.SDA, Componente3.D1_TX
  N14: Componente2.A3, Componente2.N$238
  N15: Componente2.D52, S3.Pin_1, S3.Pin_2
  N16: Componente2.D46, S1.Pin_1, S1.Pin_2
  N17: Componente2.D48, S2.Pin_1, S2.Pin_2
  N18: Componente2.D50, S4.L2
  N19: Componente2.N$82, Componente2.N$83
  N20: Componente2.N$237, Componente2.N$240

notes:
  UP - DOWN - STOP - PWR
  GND - ENAB - DIR - STEP
  to motor controller
  A+
  A-
  E+
  E-
